# Fritzing sketch STpic (saved by Fritzing 0.8.0b)
stripboards: 1

parts:
  PIC1 = PIC - 16F876A [package="DIP (Dual Inline) [THT]"]
  XTAL1 = Crystal [frequency="20 MHz" package=THT]
  C2 = Ceramic Capacitor [capacitance=20pF package="100 mil [THT, multilayer]"]
  C3 = Ceramic Capacitor [capacitance=20pF package="100 mil [THT, multilayer]"]
  C4 = Ceramic Capacitor [capacitance=100nF package="100 mil [THT, multilayer]"]
  U2 = Voltage Regulator - Variable [package="TO220 [THT]"]
  R1 = Resistor [tolerance=±5% resistance=240 package=THT]
  R2 = Resistor [tolerance=±5% resistance=220 package=THT]
  C5 = Electrolytic Capacitor [capacitance=10µF package="100 mil [THT, electrolytic]"]
  Composants1 = Logic Level Converter
  J1 = male pin header, 6 pins [form="♂ (male)"]

nets:
  N1: PIC1.#MCLR/Vpp, J1.pin1
  VSS: PIC1.Vss, C2.0, C3.1, C4.0, R2.Pin_0, C5.-, Composants1.GND, J1.pin3
  N2: PIC1.OSC1/CLKI, XTAL1.pin_0, C3.0
  N3: PIC1.OSC2/CLKO, XTAL1.pin_1, C2.1
  N4: PIC1.RC3/SCK/SCL, PIC1.RC6/TX/CK
  N5: PIC1.RC4/SDI/SDA, Composants1.TX2_HV
  N6: PIC1.RC5/SDO, Composants1.TX_HV
  N7: PIC1.Vdd, C4.1, U2.IN, Composants1.HV, J1.pin2
  N8: PIC1.RB3/PGM, J1.pin6
  N9: PIC1.RB6/PGC, J1.pin5
  N10: PIC1.RB7/PGD, J1.pin4
  N11: U2.ADJ, R1.Pin_1, R2.Pin_1
  N12: U2.OUT, R1.Pin_0, C5.+, Composants1.LV

custom parts:
  PIC - 16F876A: Microchip PIC - 16F876A
