# Fritzing sketch STpic2 (saved by Fritzing 0.8.0b)
perfboards: 1

parts:
  R1 = Resistor [tolerance=±5% resistance=4.7k package=THT]
  PIC2 = PIC - 16F876A [package="DIP (Dual Inline) [THT]"]
  C4 = Ceramic Capacitor [capacitance=100nF package="100 mil [THT, multilayer]"]
  XTAL1 = Crystal [frequency="20 MHz" package=THT]
  C5 = Ceramic Capacitor [capacitance=22pF package="100 mil [THT, multilayer]"]
  C6 = Ceramic Capacitor [capacitance=22pF package="100 mil [THT, multilayer]"]
  J3 = Screw terminal - 9 pins [package=THT]
  R2 = Resistor [tolerance=±5% resistance=470 package=THT]
  LED1 = LED - 5mm [color="Red (633nm)" package="5 mm [THT]"]
  D1 = Rectifier Diode [part_number=1N4148 package="300 mil [THT]"]
  D2 = Rectifier Diode [part_number=1N4148 package="300 mil [THT]"]
  D3 = Rectifier Diode [part_number=1N4148 package="300 mil [THT]"]
  D4 = Rectifier Diode [part_number=1N4148 package="300 mil [THT]"]
  D5 = Rectifier Diode [part_number=1N4148 package="300 mil [THT]"]
  D6 = Rectifier Diode [part_number=1N4148 package="300 mil [THT]"]
  J4 = Generic male header - 6 pins [form="♂ (male)" package=THT]
  J5 = Wii Controller Header [form="♂ (male)" package=THT]
  U1 = Voltage Regulator - Variable [package="TO220 [THT]"]
  J6 = Screw terminal - 2 pins [package=THT]
  Composants1 = Logic Level Converter
  R3 = Resistor [tolerance=±5% resistance=390 package=THT]
  R4 = Resistor [tolerance=±5% resistance=240 package=THT]
  C7 = Electrolytic Capacitor [capacitance=1µF package="100 mil [THT, electrolytic]"]
  S1 = Toggle Switch [package=THT]
  J7 = female pin header, 6 pins [form="♀ (female)"]

nets:
  VDD: R1.Pin_0, PIC2.Vdd, C4.0, J3.Vdd, LED1.anode, J4.Vdd, U1.IN, Composants1.HV, S1.COM
  N1: R1.Pin_1, PIC2.#MCLR/Vpp, J4.#MCLR/Vpp
  N2: PIC2.RA0/AN0, D1.cathode, J7.pin1
  N3: PIC2.RA1/AN1, D2.cathode, J7.pin2
  N4: PIC2.RA2/AN2/Vref-/CVref, D3.cathode, J7.pin3
  N5: PIC2.RA3/AN3/Vref+, D4.cathode, J7.pin4
  N6: PIC2.RA4/T0CKI/C1OUT, D5.cathode, J7.pin5
  N7: PIC2.RA5/AN4/#SS/C2OUT, D6.cathode, J7.pin6
  GND: PIC2.Vss, C4.1, C5.0, C6.0, J3.Gnd, R2.Pin_0, J4.Vss, J5.Gnd_(Yellow), J6.pin1, Composants1.GND, R3.Pin_0, C7.-
  N8: PIC2.OSC1/CLKI, XTAL1.pin_1, C5.1
  N9: PIC2.OSC2/CLKO, XTAL1.pin_0, C6.1
  N10: PIC2.RC3/SCK/SCL, Composants1.TX_HV
  N11: PIC2.RC4/SDI/SDA, Composants1.TX2_HV
  N12: PIC2.RB6/PGC, J4.PGC
  N13: PIC2.RB7/PGD, J4.PGD
  N14: J3.Up/Xb, D1.anode
  N15: J3.Down/Xa, D2.anode
  N16: J3.Left/Ya, D3.anode
  N17: J3.Right/Yb, D4.anode
  N18: J3.Fire/Left_Btn, D5.anode
  N19: J3.Joy1_Fire/Right_btn, D6.anode
  N20: R2.Pin_1, LED1.cathode
  N21: J5.SDA_(Brown), Composants1.TX2_LV
  N22: J5.SCL_(Red), Composants1.TX_LV
  N23: J5.V33_(Black), U1.OUT, Composants1.LV, R4.Pin_1, C7.+
  N24: U1.ADJ, R3.Pin_1, R4.Pin_0
  N25: J6.pin2, S1.L2

notes:
  STpic, Atari ST Wii <-> Joystick converter, v1.0.0

custom parts:
  PIC - 16F876A: Microchip PIC - 16F876A
  Screw terminal - 9 pins: Screw terminal with 9 pins
  Generic male header - 6 pins: Generic male header
  Wii Controller Header: Wii Controller Header (Nunchuck / Classic / ...)
