# Fritzing sketch wii2st (saved by Fritzing 0.8.0b)
breadboards: 1

parts:
  Composants1 = Logic Level Converter
  Composants2 = Arduino Uno (Rev3)
  J1 = female pin header, 4 pins [form="♀ (female)"]
  D1 = Rectifier Diode [part_number=1N4001 package="300 mil [THT]"]
  D2 = Rectifier Diode [part_number=1N4001 package="300 mil [THT]"]
  D3 = Rectifier Diode [part_number=1N4001 package="300 mil [THT]"]
  D4 = Rectifier Diode [part_number=1N4001 package="300 mil [THT]"]
  D5 = Rectifier Diode [part_number=1N4001 package="300 mil [THT]"]
  D6 = Rectifier Diode [part_number=1N4001 package="300 mil [THT]"]
  J2 = female pin header, 9 pins [form="♀ (female)"]

nets:
  N1: Composants1.TX2_LV, J1.pin3
  GND: Composants1.GND, Composants2.GND, J1.pin1, J2.pin8
  N2: Composants1.LV, Composants2.3V3, J1.pin4
  N3: Composants1.TX_LV, J1.pin2
  N4: Composants1.TX_HV, Composants2.A4/SDA
  N5: Composants1.HV, Composants2.5V, J2.pin7
  N6: Composants1.TX2_HV, Composants2.A5/SCL
  N7: Composants2.D8, D6.cathode
  N8: Composants2.D2, D1.cathode
  N9: Composants2.D3_PWM, D2.cathode
  N10: Composants2.D4, D3.cathode
  N11: Composants2.D5_PWM, D4.cathode
  N12: Composants2.D7, D5.cathode
  N13: D1.anode, J2.pin1
  N14: D2.anode, J2.pin2
  N15: D3.anode, J2.pin3
  N16: D4.anode, J2.pin4
  N17: D5.anode, J2.pin6
  N18: D6.anode, J2.pin9

notes:
  http://www.opento.me/wordpress/
  Wii Controller doc: http://wiibrew.org/wiki/Wiimote/Extension_Controllers
  Wii Controller Connector
